// Logisim project Lucas_Neves_SI4N.circ as structural Verilog: 7 circuits, main circuit main
module main (
  input  [3:0] B,
  input  [3:0] A,
  input  [2:0] in_3,
  output out_4,
  output [3:0] out_5
);

  wire dec_3x8_1_a, dec_3x8_1_b, dec_3x8_1_c, dec_3x8_1_d;
  wire [3:0] add_4_1_s, not_1_s, or_4_1_s;

  Dec_3x8 dec_3x8_1 (
    .a(dec_3x8_1_a), .b(dec_3x8_1_b), .c(dec_3x8_1_c), .d(dec_3x8_1_d), .in_1(in_3));  // open: e, f, g, h
  Buffer buffer_1 (.B(B), .C(dec_3x8_1_a), .S(out_5));
  Add_4 add_4_1 (.A(A), .out_3(out_4), .B(B), .S(add_4_1_s));
  Buffer buffer_2 (.B(add_4_1_s), .C(dec_3x8_1_b), .S(out_5));
  OR_4 or_4_1 (.A(A), .B(B), .S(or_4_1_s));
  Buffer buffer_3 (.B(or_4_1_s), .C(dec_3x8_1_c), .S(out_5));
  NOT not_1 (.B(B), .S(not_1_s));
  Buffer buffer_4 (.B(not_1_s), .C(dec_3x8_1_d), .S(out_5));
endmodule

module Add_1 (
  input  A,
  input  B,
  input  Vem_1,
  output Soma,
  output Vai_1
);

  wire and_1_out, and_2_out, and_3_out, and_4_out, and_5_out, and_6_out, and_7_out, not_1_out, not_2_out,
       not_3_out, not_4_out, not_5_out, not_6_out;

  not not_1 (not_1_out, A);
  not not_2 (not_2_out, B);
  not not_3 (not_3_out, A);
  not not_4 (not_4_out, Vem_1);
  not not_5 (not_5_out, B);
  not not_6 (not_6_out, Vem_1);
  and and_1 (and_1_out, B, Vem_1);
  and and_2 (and_2_out, A, Vem_1);
  and and_3 (and_3_out, A, B);
  and and_4 (and_4_out, not_1_out, not_2_out, Vem_1);
  and and_5 (and_5_out, not_3_out, B, not_4_out);
  and and_6 (and_6_out, A, not_5_out, not_6_out);
  and and_7 (and_7_out, A, B, Vem_1);
  or or_1 (Vai_1, and_1_out, and_2_out, and_3_out);
  or or_2 (Soma, and_4_out, and_5_out, and_6_out, and_7_out);
endmodule

module Add_4 (
  input  [3:0] B,
  input  [3:0] A,
  output out_3,
  output [3:0] S
);

  wire add_1_2_vai_1, add_1_3_vai_1, add_1_4_vai_1;

  // Probe on A
  Add_1 add_1_1 (.A(A[3]), .B(B[3]), .Vem_1(add_1_2_vai_1), .Soma(S[3]), .Vai_1(out_3));
  Add_1 add_1_2 (.A(A[2]), .B(B[2]), .Vem_1(add_1_3_vai_1), .Soma(S[2]), .Vai_1(add_1_2_vai_1));
  Add_1 add_1_3 (.A(A[1]), .B(B[1]), .Vem_1(add_1_4_vai_1), .Soma(S[1]), .Vai_1(add_1_3_vai_1));
  Add_1 add_1_4 (.A(A[0]), .B(B[0]), .Vem_1(1'b0), .Soma(S[0]), .Vai_1(add_1_4_vai_1));
endmodule

module OR_4 (
  input  [3:0] B,
  input  [3:0] A,
  output [3:0] S
);

  or or_1 (S[3], A[3], B[3]);
  or or_2 (S[2], A[2], B[2]);
  or or_3 (S[1], A[1], B[1]);
  or or_4 (S[0], A[0], B[0]);
endmodule

module NOT (
  input  [3:0] B,
  output [3:0] S
);

  not not_1 (S[2], B[2]);
  not not_2 (S[3], B[3]);
  not not_3 (S[1], B[1]);
  not not_4 (S[0], B[0]);
endmodule

module Buffer (
  input  [3:0] B,
  input  C,
  output [3:0] S
);

  assign S[2] = C ? B[2] : 1'bz;  // Controlled_Buffer controlled_buffer_1
  assign S[3] = C ? B[3] : 1'bz;  // Controlled_Buffer controlled_buffer_2
  assign S[1] = C ? B[1] : 1'bz;  // Controlled_Buffer controlled_buffer_3
  assign S[0] = C ? B[0] : 1'bz;  // Controlled_Buffer controlled_buffer_4
endmodule

module Dec_3x8 (
  input  [2:0] in_1,
  output a,
  output b,
  output c,
  output d,
  output e,
  output f,
  output g,
  output h
);

  wire not_1_out, not_2_out, not_3_out, not_4_out, not_5_out, not_6_out, not_7_out, not_8_out, not_9_out,
       not_10_out, not_11_out, not_12_out;

  not not_1 (not_1_out, in_1[2]);
  not not_2 (not_2_out, in_1[1]);
  not not_3 (not_3_out, in_1[0]);
  not not_4 (not_4_out, in_1[2]);
  not not_5 (not_5_out, in_1[1]);
  not not_6 (not_6_out, in_1[2]);
  not not_7 (not_7_out, in_1[0]);
  not not_8 (not_8_out, in_1[2]);
  not not_9 (not_9_out, in_1[1]);
  not not_10 (not_10_out, in_1[0]);
  not not_11 (not_11_out, in_1[1]);
  not not_12 (not_12_out, in_1[0]);
  and and_1 (h, in_1[2], in_1[1], in_1[0]);
  and and_2 (a, not_1_out, not_2_out, not_3_out);
  and and_3 (b, not_4_out, not_5_out, in_1[0]);
  and and_4 (c, not_6_out, in_1[1], not_7_out);
  and and_5 (d, not_8_out, in_1[1], in_1[0]);
  and and_6 (e, in_1[2], not_9_out, not_10_out);
  and and_7 (f, in_1[2], not_11_out, in_1[0]);
  and and_8 (g, in_1[2], in_1[1], not_12_out);
endmodule
